# Fritzing sketch 1-BrightnessCtrl-UNO (saved by Fritzing 1.0.6)
breadboards: 1

parts:
  R1 = Resistor [tolerance=±5% power=0.25W resistance=220 package=THT]
  R2 = Resistor [tolerance=±5% power=0.25W resistance=220 package=THT]
  LED1 = LED - 5mm [color="Green (555nm)" current=0.030A package="5 mm [THT]"]
  LED2 = LED - 5mm [color="Red (633nm)" current=0.030A package="5 mm [THT]"]
  R3 = Resistor [tolerance=±5% power=0.25W resistance=220 package=THT]
  Part1 = Arduino Uno (Rev3) - ICSP
  LED3 = LED - 5mm [color="Yellow (595nm)" current=0.030A package="5 mm [THT]"]
  R4 = Resistor [tolerance=±5% power=0.25W resistance=220 package=THT]
  R5 = Rotary Potentiometer (Small) [maximum_resistance=10kΩ knob_status=50% power=0.5W package=THT]

nets:
  N1: R1.Pin_0, Part1.D7, R5.leg1
  N2: R1.Pin_1, Part1.5V
  N3: R2.Pin_0, LED1.anode
  N4: R2.Pin_1, Part1.D5_PWM
  N5: LED1.cathode, LED2.cathode, Part1.GND, LED3.cathode, R5.leg2
  N6: LED2.anode, R3.Pin_0
  N7: R3.Pin_1, Part1.D3_PWM
  N8: Part1.A0, R5.wiper
  N9: Part1.D6_PWM, R4.Pin_1
  N10: LED3.anode, R4.Pin_0

// code stored in the sketch: Untitled.ino
#include <Arduino.h>


#define ledRed 2
#define ledGreen 4
#define buttonSpeedUp 6


void setup() {
  // put your setup code here, to run once:
  Serial.begin(9600);
  pinMode(buttonSpeedUp, INPUT);
  digitalWrite(buttonSpeedUp, HIGH);


  pinMode(ledRed, OUTPUT);
  pinMode(ledGreen, OUTPUT);
}


void speedMode(int option){
  if (option == 1){
    digitalWrite(ledRed, HIGH);
    delay(100);
    digitalWrite(ledRed, LOW);
    digitalWrite(ledGreen, HIGH);
    delay(100);
    digitalWrite(ledGreen, LOW);
  } else {
    digitalWrite(ledRed, HIGH);
    delay(5000);
    digitalWrite(ledRed, LOW);
    digitalWrite(ledGreen, HIGH);
    delay(5000);
    digitalWrite(ledGreen, LOW);
  }
}


void loop() {
  // put your main code here, to run repeatedly:
  int isButtonSpeedPressed = digitalRead(buttonSpeedUp);


  if(isButtonSpeedPressed == 0){
    Serial.println("Haloo kawan");
    speedMode(1);
  } else {
    speedMode(0);
  }
}
